# Fritzing sketch PoorManMacros (saved by Fritzing 0.9.10b)
circuit board: 2.42837cm x 2.59116cm
breadboards: 1

parts:
  A1 = Waveshare rp2040-zero tht [package=THT]
  Keypad4x1 = Keypad Membran 4x4

nets:
  N1: A1.Pin_16, Keypad4x1.Pin8
  N2: A1.Pin_17, Keypad4x1.Pin7
  N3: A1.Pin_18, Keypad4x1.Pin6
  N4: A1.Pin_19, Keypad4x1.Pin5
  N5: A1.Pin_20, Keypad4x1.Pin4
  N6: A1.Pin_21, Keypad4x1.Pin3
  N7: A1.Pin_22, Keypad4x1.Pin2
  N8: A1.Pin_23, Keypad4x1.Pin1

custom parts:
  Waveshare rp2040-zero tht: .RP2040-Zero, A Low-Cost, High-Performance Pico-Like MCU Board Based On Raspberry Pi Microcontroller RP2040. This varant is THT without the extra connections.
  Keypad Membran 4x4: Membrane Keypad 4x4 Matrix
