# Fritzing sketch PoorManMacros_12mm_switch_IndividualPins (saved by Fritzing 0.9.10b)
circuit board: 10cm x 6.5cm
breadboards: 4

parts:
  A1 = Waveshare rp2040-zero tht [package=THT]
  S17 = SWITCH-MOMENTARY-12mm [package=tactile-pth-12mm]
  S18 = SWITCH-MOMENTARY-12mm [package=tactile-pth-12mm]
  S19 = SWITCH-MOMENTARY-12mm [package=tactile-pth-12mm]
  S20 = SWITCH-MOMENTARY-12mm [package=tactile-pth-12mm]
  S21 = SWITCH-MOMENTARY-12mm [package=tactile-pth-12mm]
  S22 = SWITCH-MOMENTARY-12mm [package=tactile-pth-12mm]
  S23 = SWITCH-MOMENTARY-12mm [package=tactile-pth-12mm]
  S24 = SWITCH-MOMENTARY-12mm [package=tactile-pth-12mm]
  S25 = SWITCH-MOMENTARY-12mm [package=tactile-pth-12mm]
  S26 = SWITCH-MOMENTARY-12mm [package=tactile-pth-12mm]
  S27 = SWITCH-MOMENTARY-12mm [package=tactile-pth-12mm]
  S28 = SWITCH-MOMENTARY-12mm [package=tactile-pth-12mm]
  S29 = SWITCH-MOMENTARY-12mm [package=tactile-pth-12mm]
  S31 = SWITCH-MOMENTARY-12mm [package=tactile-pth-12mm]
  S32 = SWITCH-MOMENTARY-12mm [package=tactile-pth-12mm]
  Z1 = VARISTOR [package=0603-res]
  Z2 = VARISTOR [package=0603-res]
  Z3 = VARISTOR [package=0603-res]
  Z4 = VARISTOR [package=0603-res]
  Z5 = VARISTOR [package=0603-res]
  Z6 = VARISTOR [package=0603-res]
  Z7 = VARISTOR [package=0603-res]
  Z8 = VARISTOR [package=0603-res]
  Z9 = VARISTOR [package=0603-res]
  Z10 = VARISTOR [package=0603-res]
  Z11 = VARISTOR [package=0603-res]
  Z13 = VARISTOR [package=0603-res]
  Z14 = VARISTOR [package=0603-res]
  Z15 = VARISTOR [package=0603-res]
  Z16 = VARISTOR [package=0603-res]
  Z12 = VARISTOR [package=0603-res]
  S30 = SWITCH-MOMENTARY-12mm [package=tactile-pth-12mm]

nets:
  N1: A1.Pin_2, S17.1, S18.1, S19.1, S20.1, S21.1, S22.1, S23.1, S24.1, S25.1, S26.1, S27.1, S28.1, S29.1, S31.1, S32.1, S30.1
  N2: A1.Pin_3, Z1.2, Z2.2, Z3.2, Z4.2, Z5.2, Z6.2, Z7.2, Z8.2, Z9.2, Z10.2, Z11.2, Z13.2, Z14.2, Z15.2, Z16.2, Z12.2
  N3: A1.Pin_8, S32.2, Z16.1
  N4: A1.Pin_9, S31.2, Z15.1
  N5: A1.Pin_10, Z14.1, S30.2
  N6: A1.Pin_11, S29.2, Z13.1
  N7: A1.Pin_12, S28.2, Z12.1
  N8: A1.Pin_13, S27.2, Z11.1
  N9: A1.Pin_14, S26.2, Z10.1
  N10: A1.Pin_15, S25.2, Z9.1
  N11: A1.Pin_16, S24.2, Z8.1
  N12: A1.Pin_17, S23.2, Z7.1
  N13: A1.Pin_18, S22.2, Z6.1
  N14: A1.Pin_19, S21.2, Z5.1
  N15: A1.Pin_20, S20.2, Z4.1
  N16: A1.Pin_21, S19.2, Z3.1
  N17: A1.Pin_22, S18.2, Z2.1
  N18: A1.Pin_23, S17.2, Z1.1

notes:
  Andrew Bowman
  2024

custom parts:
  Waveshare rp2040-zero tht: .RP2040-Zero, A Low-Cost, High-Performance Pico-Like MCU Board Based On Raspberry Pi Microcontroller RP2040. This varant is THT without the extra connections.
  SWITCH-MOMENTARY-12mm: Various NO switches- pushbuttons, reed, etc
